# Fritzing sketch 2_TwoBlinkBrighter (saved by Fritzing 0.9.3b)
breadboards: 1

parts:
  부품1 = Arduino Uno (Rev3)
  LED1 = LED - 5mm [color="Red (633nm)" package="5 mm [THT]"]
  R1 = Resistor [tolerance=±5% resistance=220 package=THT]
  LED2 = LED - 5mm [color="Green (570nm)" package="5 mm [THT]"]
  R2 = Resistor [tolerance=±5% resistance=220 package=THT]

nets:
  N1: 부품1.D5_PWM, LED2.anode
  N2: 부품1.D6_PWM, LED1.anode
  N3: 부품1.GND, R1.Pin_0, R2.Pin_0
  N4: LED1.cathode, R1.Pin_1
  N5: LED2.cathode, R2.Pin_1
