# Fritzing sketch 6_VariableResistor (saved by Fritzing 0.9.3b)
breadboards: 1

parts:
  부품1 = Arduino Uno (Rev3)
  R1 = Trimmer Potentiometer [maximum_resistance=10kΩ package=THT]
  LED1 = LED - 5mm [color="Red (633nm)" package="5 mm [THT]"]
  R2 = Resistor [tolerance=±5% resistance=220 package=THT]

nets:
  N1: 부품1.A0, R1.wiper
  N2: 부품1.D11_PWM/MOSI, LED1.anode
  N3: 부품1.GND, R1.leg1, R2.Pin_0
  N4: 부품1.5V, R1.leg2
  N5: LED1.cathode, R2.Pin_1
