# Fritzing sketch 16_Distance_Speaker (saved by Fritzing 0.9.3b)
breadboards: 1

parts:
  부품1 = Arduino Uno (Rev3)
  hc-sr1 = hc-sr04
  J1 = Piezo Speaker

nets:
  N1: 부품1.D10_PWM/SS, J1.pin2
  N2: 부품1.D11_PWM/MOSI, hc-sr1.Echo
  N3: 부품1.D12/MISO, hc-sr1.Trig
  5V: 부품1.5V, hc-sr1.VCC, J1.pin1
  GND: 부품1.GND, hc-sr1.GND
