# Fritzing sketch 18_Potentiometer_Servo_Motor (saved by Fritzing 0.9.3b)
breadboards: 1

parts:
  부품1 = Arduino Uno (Rev3)
  J1 = Basic Servo
  R1 = Trimmer Potentiometer [maximum_resistance=10kΩ package=THT]

nets:
  N1: 부품1.D10_PWM/SS, R1.wiper
  N2: 부품1.D3_PWM, J1.pulse
  5V: 부품1.5V, J1.vcc, R1.leg2
  GND: 부품1.GND, J1.gnd, R1.leg1
