# Fritzing sketch 19_Servo_Motor_Distance_Sensor (saved by Fritzing 0.9.3b)
breadboards: 1

parts:
  부품1 = Arduino Uno (Rev3)
  J1 = Basic Servo
  hc-sr1 = hc-sr04

nets:
  N1: 부품1.D11_PWM/MOSI, hc-sr1.Echo
  N2: 부품1.D12/MISO, hc-sr1.Trig
  N3: 부품1.D3_PWM, J1.pulse
  VCC: 부품1.5V, J1.vcc, hc-sr1.VCC
  GND: 부품1.GND, J1.gnd, hc-sr1.GND
