# Fritzing sketch 4_ButtonKeepBright (saved by Fritzing 0.9.3b)
breadboards: 1

parts:
  부품1 = Arduino Uno (Rev3)
  LED1 = LED - 5mm [color="Red (633nm)" package="5 mm [THT]"]
  R1 = Resistor [tolerance=±5% resistance=220 package=THT]
  S1 = Pushbutton [package="[THT]"]
  R2 = Resistor [tolerance=±5% resistance=10k package=THT]

nets:
  N1: 부품1.D10_PWM/SS, S1.Pin_1, S1.Pin_2, R2.Pin_1
  N2: 부품1.D12/MISO, LED1.anode
  N3: 부품1.5V, S1.Pin_3, S1.Pin_4
  N4: 부품1.GND, R1.Pin_0, R2.Pin_0
  N5: LED1.cathode, R1.Pin_1
