# Fritzing sketch 7_RGBLed_ThreeButtons (saved by Fritzing 0.9.3b)
breadboards: 1

parts:
  부품1 = Arduino Uno (Rev3)
  LED1 = RGB LED (com. cathode, rgb) [package="5 mm [THT]"]
  R1 = Resistor [tolerance=±5% resistance=220 package=THT]
  R2 = Resistor [tolerance=±5% resistance=220 package=THT]
  R3 = Resistor [tolerance=±5% resistance=220 package=THT]
  R4 = Resistor [tolerance=±5% resistance=10k package=THT]
  R5 = Resistor [tolerance=±5% resistance=10k package=THT]
  S1 = Pushbutton [package="[THT]"]
  S2 = Pushbutton [package="[THT]"]
  S3 = Pushbutton [package="[THT]"]
  R6 = Resistor [tolerance=±5% resistance=10k package=THT]

nets:
  N1: 부품1.D9_PWM, R3.Pin_0
  N2: 부품1.D10_PWM/SS, R2.Pin_0
  N3: 부품1.D11_PWM/MOSI, R1.Pin_0
  N4: 부품1.D3_PWM, S3.Pin_1, S3.Pin_2, R6.Pin_1
  N5: 부품1.D4, R5.Pin_1, S2.Pin_1, S2.Pin_2
  N6: 부품1.D5_PWM, R4.Pin_1, S1.Pin_1, S1.Pin_2
  N7: 부품1.5V, S1.Pin_3, S1.Pin_4, S2.Pin_3, S2.Pin_4, S3.Pin_3, S3.Pin_4
  N8: 부품1.GND, LED1.common_cathode, R4.Pin_0, R5.Pin_0, R6.Pin_0
  N9: LED1.red_anode, R1.Pin_1
  N10: LED1.green_anode, R2.Pin_1
  N11: LED1.blue_anode, R3.Pin_1
